# Fritzing sketch 01. DHT11 - Diagram (saved by Fritzing 1.0.4)
breadboards: 1

parts:
  Part1 = Arduino Uno (Rev3)
  DHT1 = DHT11 Humitidy and Temperature Sensor
  R1 = Resistor [tolerance=±5% resistance=10k package="1206 [SMD]"]
  A1 = MH breadboard power supply module

nets:
  N1: Part1.D2, DHT1.DATA, R1.Pin_0
  GND: Part1.GND, DHT1.GND, A1.Pin_1, A1.Pin_2, A1.Pin_3, A1.Pin_7, A1.Pin_8, A1.Pin_9
  VIN: Part1.VIN, DHT1.VDD, R1.Pin_1, A1.Pin_10, A1.Pin_11, A1.Pin_12
  N2: A1.Pin_4, A1.Pin_5, A1.Pin_6

custom parts:
  DHT11 Humitidy and Temperature Sensor: DHT11 Humidity and Temperature Sensor
